# Fritzing sketch Datalogger Module (saved by Fritzing 0.9.2b)
circuit board: 8.46667cm x 5.64444cm
breadboards: 1

parts:
  Onderdeel1 = Arduino Uno (Rev3)
  LED2 = LED - 5mm [color="Red (633nm)" package="5 mm [THT]"]
  LED3 = LED - 5mm [color="Red (633nm)" package="5 mm [THT]"]
  R1 = Resistor [tolerance=±5% resistance=220 package="0402 [SMD]"]
  S1 = Momentary Switch [package=tactile_switch_smd]
  LED4 = LED - 5mm [color="Red (633nm)" package="5 mm [THT]"]
  R1_2 = Resistor [tolerance=±5% resistance=1M package=THT]
  R2 = Resistor [tolerance=±5% resistance=1M package=THT]

nets:
  N1: Onderdeel1.A5/SCL, R1_2.Pin_1, R2.Pin_0
  N2: Onderdeel1.D8, S1.2
  N3: Onderdeel1.D2, LED4.anode
  N4: Onderdeel1.D4, LED2.anode
  N5: Onderdeel1.D7, LED3.anode
  N6: Onderdeel1.5V, S1.3
  N7: Onderdeel1.GND, R1.Pin_0, S1.1, R2.Pin_1
  N8: LED2.cathode, LED3.cathode, R1.Pin_1, LED4.cathode

notes:
  Unpressed: LOW
  Pressed: HIGH
  Apply max. 10V here to measure voltage. Increase resistor R2 relative to R1 if more voltage needs to be measured. Power on pin A5 should not exceed 5V.
